# Fritzing sketch ball lock schematic (saved by Fritzing 0.8.7b)

parts:
  Part1 = Arduino Uno (Rev3)
  Part2 = Adafruit PCA9685 PWM/Servo Breakout [part_number=815]
  J1 = Basic Servo
  J5 = Power Jack [package=power_jack_pth_lock]

nets:
  N1: Part1.A4/SDA, Part2.SDA
  N2: Part1.A5/SCL, Part2.SCL
  5V: Part1.5V, Part2.VCC
  GND: Part1.GND, Part2.GND, J1.gnd, J5.GND
  N3: Part2.PWRIN, J5.PWR
  N4: Part2.PWM0, J1.pulse
  N5: Part2.5.0V, J1.vcc

custom parts:
  Adafruit PCA9685 PWM/Servo Breakout: Using only two pins, control 16 free-running PWM outputs! I2C-controlled PWM driver with a built in clock. Unlike the TLC5940 family, you do not need to continuously send it signal tying up your microcontroller, its completely free running! 5V compliant, which means you can control it from a 3.3V microcontroller and still safely drive up to 6V outputs (this is good for when you want to control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
